// Logisim project Najifa Tabassum_2211578042_sec4_lab6.circ as structural Verilog: 4 circuits, main circuit main
module main (
  input  A,
  input  B,
  input  [1:0] in_3,
  input  Cin,
  input  Binv,
  output out_6,
  output Cout
);

  wire adder_1_out, and_1_out, multiplexer_1_out, nor_1_out, not_1_out;

  not not_1 (not_1_out, B);
  and and_1 (and_1_out, A, B);
  Multiplexer #(.enable("false")) multiplexer_1 (.in0(B), .in1(not_1_out), .out(multiplexer_1_out), .sel(Binv));
  nor nor_1 (nor_1_out, A, B);
  Adder #(.width(1)) adder_1 (.a(A), .b(multiplexer_1_out), .out(adder_1_out), .cin(Cin), .cout(Cout));
  Multiplexer #(.select(2), .enable("false")) multiplexer_2 (
    .in0(and_1_out), .in1(nor_1_out), .in2(adder_1_out), .in3(adder_1_out), .out(out_6), .sel(in_3));
endmodule

module _16_bit_ALU (
  input  Binv,
  input  [15:0] B,
  input  Cin,
  input  [15:0] A,
  input  [1:0] Selection_control,
  output [15:0] Result,
  output Cout,
  output Zero_Flag
);

  wire main_1_cout, main_3_cout, main_4_cout, main_5_cout, main_6_cout, main_7_cout, main_8_cout,
       main_9_cout, main_10_cout, main_11_cout, main_12_cout, main_13_cout, main_14_cout, main_15_cout,
       main_16_cout;

  main main_1 (
    .Cin(Cin), .out_6(Result[0]), .A(A[0]), .B(B[0]), .Binv(Binv), .Cout(main_1_cout),
    .in_3(Selection_control));
  main main_2 (
    .Cin(main_4_cout), .out_6(Result[15]), .A(A[15]), .B(B[15]), .Binv(Binv), .Cout(Cout),
    .in_3(Selection_control));
  main main_3 (
    .Cin(main_1_cout), .out_6(Result[1]), .A(A[1]), .B(B[1]), .Binv(Binv), .Cout(main_3_cout),
    .in_3(Selection_control));
  main main_4 (
    .Cin(main_6_cout), .out_6(Result[14]), .A(A[14]), .B(B[14]), .Binv(Binv), .Cout(main_4_cout),
    .in_3(Selection_control));
  main main_5 (
    .Cin(main_3_cout), .out_6(Result[2]), .A(A[2]), .B(B[2]), .Binv(Binv), .Cout(main_5_cout),
    .in_3(Selection_control));
  main main_6 (
    .Cin(main_8_cout), .out_6(Result[13]), .A(A[13]), .B(B[13]), .Binv(Binv), .Cout(main_6_cout),
    .in_3(Selection_control));
  main main_7 (
    .Cin(main_5_cout), .out_6(Result[3]), .A(A[3]), .B(B[3]), .Binv(Binv), .Cout(main_7_cout),
    .in_3(Selection_control));
  main main_8 (
    .Cin(main_10_cout), .out_6(Result[12]), .A(A[12]), .B(B[12]), .Binv(Binv), .Cout(main_8_cout),
    .in_3(Selection_control));
  main main_9 (
    .Cin(main_7_cout), .out_6(Result[4]), .A(A[4]), .B(B[4]), .Binv(Binv), .Cout(main_9_cout),
    .in_3(Selection_control));
  main main_10 (
    .Cin(main_12_cout), .out_6(Result[11]), .A(A[11]), .B(B[11]), .Binv(Binv), .Cout(main_10_cout),
    .in_3(Selection_control));
  main main_11 (
    .Cin(main_9_cout), .out_6(Result[5]), .A(A[5]), .B(B[5]), .Binv(Binv), .Cout(main_11_cout),
    .in_3(Selection_control));
  main main_12 (
    .Cin(main_14_cout), .out_6(Result[10]), .A(A[10]), .B(B[10]), .Binv(Binv), .Cout(main_12_cout),
    .in_3(Selection_control));
  main main_13 (
    .Cin(main_11_cout), .out_6(Result[6]), .A(A[6]), .B(B[6]), .Binv(Binv), .Cout(main_13_cout),
    .in_3(Selection_control));
  main main_14 (
    .Cin(main_16_cout), .out_6(Result[9]), .A(A[9]), .B(B[9]), .Binv(Binv), .Cout(main_14_cout),
    .in_3(Selection_control));
  main main_15 (
    .Cin(main_13_cout), .out_6(Result[7]), .A(A[7]), .B(B[7]), .Binv(Binv), .Cout(main_15_cout),
    .in_3(Selection_control));
  main main_16 (
    .Cin(main_15_cout), .out_6(Result[8]), .A(A[8]), .B(B[8]), .Binv(Binv), .Cout(main_16_cout),
    .in_3(Selection_control));
  nor nor_1 (Zero_Flag, Result[0], Result[1], Result[2], Result[3], Result[4], Result[5], Result[6], Result[7], Result[8], Result[9], Result[10], Result[11], Result[12], Result[13], Result[14], Result[15]);

  // Notes on the sheet:
  //   0
  //   1 bit
  //   ALU
  //   15
  //   1 bit
  //   ALU
  //   1
  //   1 bit
  //   ALU
  //   14
  //   1 bit
  //   ALU
  //   2
  //   1 bit
  //   ALU
  //   13
  //   1 bit
  //   ALU
  //   3
  //   1 bit
  //   ALU
  //   12
  //   1 bit
  //   ALU
  //   4
  //   1 bit
  //   ALU
  //   11
  //   1 bit
  //   ALU
  //   Najifa tabassum
  //   2211578042
  //   5
  //   1 bit
  //   ALU
  //   10
  //   1 bit
  //   ALU
  //   6
  //   1 bit
  //   ALU
  //   9
  //   1 bit
  //   ALU
  //   7
  //   1 bit
  //   ALU
  //   8
  //   1 bit
  //   ALU
endmodule

module _16_bit_ISA (
  input  [3:0] Read_Register1,
  input  [3:0] Write_Register,
  input  Write_control,
  input  [15:0] Write_Data,
  input  clear,
  input  Clock,
  input  [3:0] Read_Register2,
  output [15:0] Read_Data1,
  output [15:0] Read_Data2
);

  wire and_1_out, and_2_out, and_3_out, and_4_out, and_5_out, and_6_out, and_7_out, and_8_out, and_9_out,
       and_10_out, and_11_out, and_12_out, and_13_out, and_14_out, and_15_out, and_16_out, decoder_1_out0,
       decoder_1_out1, decoder_1_out2, decoder_1_out3, decoder_1_out4, decoder_1_out5, decoder_1_out6,
       decoder_1_out7, decoder_1_out8, decoder_1_out9, decoder_1_out10, decoder_1_out11, decoder_1_out12,
       decoder_1_out13, decoder_1_out14, decoder_1_out15;
  wire [15:0] _0_q, _1_q, _2_q, _3_q, _4_q, _5_q, _6_q, _7_q, _8_q, _9_q, _10_q, _11_q, _12_q, _13_q, _14_q,
       _15_q;

  Decoder #(.select(4), .enable("false")) decoder_1 (
    .out0(decoder_1_out0), .out1(decoder_1_out1), .out2(decoder_1_out2), .out3(decoder_1_out3),
    .out4(decoder_1_out4), .out5(decoder_1_out5), .out6(decoder_1_out6), .out7(decoder_1_out7),
    .out8(decoder_1_out8), .out9(decoder_1_out9), .out10(decoder_1_out10), .out11(decoder_1_out11),
    .out12(decoder_1_out12), .out13(decoder_1_out13), .out14(decoder_1_out14), .out15(decoder_1_out15),
    .sel(Write_Register));
  and and_1 (and_1_out, decoder_1_out0, Write_control);
  and and_2 (and_2_out, decoder_1_out1, Write_control);
  and and_3 (and_3_out, decoder_1_out2, Write_control);
  and and_4 (and_4_out, decoder_1_out3, Write_control);
  and and_5 (and_5_out, decoder_1_out4, Write_control);
  and and_6 (and_6_out, decoder_1_out5, Write_control);
  and and_7 (and_7_out, decoder_1_out6, Write_control);
  and and_8 (and_8_out, decoder_1_out7, Write_control);
  Register #(.width(16)) _0 (.D(Write_Data), .en(and_1_out), .Q(_0_q), .clk(Clock), .clr(clear));
  Register #(.width(16)) _1 (.D(Write_Data), .en(and_2_out), .Q(_1_q), .clk(Clock), .clr(clear));
  Register #(.width(16)) _2 (.D(Write_Data), .en(and_3_out), .Q(_2_q), .clk(Clock), .clr(clear));
  Register #(.width(16)) _3 (.D(Write_Data), .en(and_4_out), .Q(_3_q), .clk(Clock), .clr(clear));
  Register #(.width(16)) _4 (.en(and_5_out), .Q(_4_q), .clk(Clock), .clr(clear));  // open: D
  Register #(.width(16)) _5 (.en(and_6_out), .Q(_5_q), .clk(Clock), .clr(clear));  // open: D
  Register #(.width(16)) _6 (.D(Write_Data), .en(and_7_out), .Q(_6_q), .clk(Clock), .clr(clear));
  Register #(.width(16)) _7 (.D(Write_Data), .en(and_8_out), .Q(_7_q), .clk(Clock), .clr(clear));
  and and_9 (and_9_out, decoder_1_out8, Write_control);
  and and_10 (and_10_out, decoder_1_out9, Write_control);
  and and_11 (and_11_out, decoder_1_out10, Write_control);
  and and_12 (and_12_out, decoder_1_out11, Write_control);
  and and_13 (and_13_out, decoder_1_out12, Write_control);
  and and_14 (and_14_out, decoder_1_out13, Write_control);
  and and_15 (and_15_out, decoder_1_out14, Write_control);
  and and_16 (and_16_out, decoder_1_out15, Write_control);
  Register #(.width(16)) _8 (.D(Write_Data), .en(and_9_out), .Q(_8_q), .clk(Clock), .clr(clear));
  Register #(.width(16)) _9 (.D(Write_Data), .en(and_10_out), .Q(_9_q), .clk(Clock), .clr(clear));
  Register #(.width(16)) _10 (.D(Write_Data), .en(and_11_out), .Q(_10_q), .clk(Clock), .clr(clear));
  Register #(.width(16)) _11 (.D(Write_Data), .en(and_12_out), .Q(_11_q), .clk(Clock), .clr(clear));
  Register #(.width(16)) _12 (.D(Write_Data), .en(and_13_out), .Q(_12_q), .clk(Clock), .clr(clear));
  Register #(.width(16)) _13 (.D(Write_Data), .en(and_14_out), .Q(_13_q), .clk(Clock), .clr(clear));
  Register #(.width(16)) _14 (.D(Write_Data), .en(and_15_out), .Q(_14_q), .clk(Clock), .clr(clear));
  Register #(.width(16)) _15 (.D(Write_Data), .en(and_16_out), .Q(_15_q), .clk(Clock), .clr(clear));
  Multiplexer #(.select(4), .width(16), .enable("false")) multiplexer_1 (
    .in0(_0_q), .in1(_1_q), .in2(_2_q), .in3(_3_q), .in4(_4_q), .in5(_5_q), .in6(_6_q), .in7(_7_q),
    .in8(_8_q), .in9(_9_q), .in10(_10_q), .in11(_11_q), .in12(_12_q), .in13(_13_q), .in14(_14_q),
    .in15(_15_q), .out(Read_Data1), .sel(Read_Register1));
  Multiplexer #(.select(4), .width(16), .enable("false")) multiplexer_2 (
    .in0(_0_q), .in1(_1_q), .in2(_2_q), .in3(_3_q), .in4(_4_q), .in5(_5_q), .in6(_6_q), .in7(_7_q),
    .in8(_8_q), .in9(_9_q), .in10(_11_q), .in11(_12_q), .in12(_12_q), .in13(_13_q), .in14(_14_q),
    .in15(_15_q), .out(Read_Data2), .sel(Read_Register2));

  // Notes on the sheet:
  //   Najifa Tabassum 
  //   Najifa tabassum
  //   2211578042
  //   2211578042
endmodule

module lab7 (
  input  MemToReg,
  input  Jump,
  input  RegDest,
  input  in_4,
  input  ALUSrc,
  input  Branch
);

  wire and_1_out, Clock_out, n16_bit_alu_1_zero_flag;
  wire [3:0] multiplexer_1_out;
  wire [15:0] adder_1_out, bit_extender_1_out, bit_extender_2_out, bit_extender_3_out, multiplexer_2_out,
       multiplexer_3_out, multiplexer_4_out, multiplexer_5_out, n16_bit_alu_1_result,
       n16_bit_isa_1_read_data1, n16_bit_isa_1_read_data2, PC_q, ram_1_data, rom_1_data;

  assign bit_extender_1_out = {{15{1'b0}}, 1'b1};  // Bit_Extender bit_extender_1
  Register #(.width(16)) PC (.D(multiplexer_4_out), .Q(PC_q), .clk(Clock_out));  // open: en, clr
  Clock Clock (.out(Clock_out));
  Adder #(.width(16)) adder_1 (.a(bit_extender_1_out), .b(PC_q), .out(adder_1_out));  // open: cin, cout
  ROM #(.addrWidth(16), .dataWidth(16)) rom_1 (.addr(PC_q), .data(rom_1_data));  // open: sel
  assign bit_extender_2_out = {{4{1'b0}}, rom_1_data[11:0]};  // Bit_Extender bit_extender_2
  Multiplexer #(.width(4), .enable("false")) multiplexer_1 (
    .in0(rom_1_data[3:0]), .in1(rom_1_data[7:4]), .out(multiplexer_1_out), .sel(RegDest));
  assign bit_extender_3_out = {{12{1'b0}}, rom_1_data[3:0]};  // Bit_Extender bit_extender_3
  _16_bit_ISA u_16_bit_isa_1 (
    .Read_Data1(n16_bit_isa_1_read_data1), .Read_Data2(n16_bit_isa_1_read_data2),
    .Write_Register(multiplexer_1_out), .Write_Data(multiplexer_5_out), .clear(in_4),
    .Read_Register1(rom_1_data[11:8]), .Read_Register2(rom_1_data[7:4]), .Clock(Clock_out));  // open: Write_control
  Multiplexer #(.width(16), .enable("false")) multiplexer_2 (
    .in0(n16_bit_isa_1_read_data2), .in1(bit_extender_3_out), .out(multiplexer_2_out), .sel(ALUSrc));
  Multiplexer #(.width(16), .enable("false")) multiplexer_3 (
    .in0(adder_1_out), .in1(bit_extender_3_out), .out(multiplexer_3_out), .sel(and_1_out));
  and and_1 (and_1_out, Branch, n16_bit_alu_1_zero_flag);
  _16_bit_ALU u_16_bit_alu_1 (
    .B(multiplexer_2_out), .Result(n16_bit_alu_1_result), .A(n16_bit_isa_1_read_data1),
    .Zero_Flag(n16_bit_alu_1_zero_flag));  // open: Binv, Cin, Cout, Selection_control
  Multiplexer #(.width(16), .enable("false")) multiplexer_4 (
    .in0(multiplexer_3_out), .in1(bit_extender_2_out), .out(multiplexer_4_out), .sel(Jump));
  RAM #(.addrWidth(16), .dataWidth(16), .bus("separate")) ram_1 (
    .addr(n16_bit_alu_1_result), .din(n16_bit_isa_1_read_data2), .data(ram_1_data), .clk(Clock_out));  // open: str, sel, ld, clr
  Multiplexer #(.width(16), .enable("false")) multiplexer_5 (
    .in0(n16_bit_alu_1_result), .in1(ram_1_data), .out(multiplexer_5_out), .sel(MemToReg));

  // Notes on the sheet:
  //   rd
  //   rt
  //   rs
  //   opcode
  //   Immediate
  //   Write Data
  //   Najifa tabassum
  //   2211578042
endmodule
