// Logisim project lab3.circ as structural Verilog: 1 circuit, main circuit main
module main (
  input  CLR,
  input  [1:0] S1,
  input  I4,
  input  I3,
  input  I2,
  input  I1,
  input  SHL,
  input  SHR,
  output A4,
  output A3,
  output A2,
  output A1
);

  wire clk_out, multiplexer_1_out, multiplexer_2_out, multiplexer_3_out, multiplexer_4_out;

  Clock clk (.out(clk_out));
  D_Flip_Flop d_ff_1 (.D(multiplexer_1_out), .clk(clk_out), .Q(A4), .reset(CLR));  // open: Qn, preset
  Multiplexer #(.select(2)) multiplexer_1 (.in0(A4), .in1(SHR), .in2(A3), .in3(I4), .out(multiplexer_1_out), .sel(S1));
  D_Flip_Flop d_ff_2 (.D(multiplexer_2_out), .clk(clk_out), .Q(A3), .reset(CLR));  // open: Qn, preset
  Multiplexer #(.select(2)) multiplexer_2 (.in0(A3), .in1(A4), .in2(A2), .in3(I3), .out(multiplexer_2_out), .sel(S1));
  D_Flip_Flop d_ff_3 (.D(multiplexer_3_out), .clk(clk_out), .Q(A2), .reset(CLR));  // open: Qn, preset
  Multiplexer #(.select(2)) multiplexer_3 (.in0(A2), .in1(A3), .in2(A1), .in3(I2), .out(multiplexer_3_out), .sel(S1));
  D_Flip_Flop d_ff_4 (.D(multiplexer_4_out), .clk(clk_out), .Q(A1), .reset(CLR));  // open: Qn, preset
  Multiplexer #(.select(2)) multiplexer_4 (.in0(A1), .in1(A2), .in2(SHL), .in3(I1), .out(multiplexer_4_out), .sel(S1));

  // Notes on the sheet:
  //   S0
  //   Najifa Tabassum
  //   2211578042
endmodule
