// Logisim project lab5.circ as structural Verilog: 1 circuit, main circuit main
module main (
  input  [3:0] Read_Register1,
  input  [3:0] Write_Register,
  input  [3:0] Read_Register2,
  input  Clear,
  input  Write_Control,
  input  [15:0] Write_Data,
  output [15:0] Read_Data1,
  output [15:0] Read_Data2
);

  wire and_1_out, and_2_out, and_3_out, and_4_out, and_5_out, and_6_out, and_7_out, and_8_out, and_9_out,
       and_10_out, and_11_out, and_12_out, and_13_out, and_14_out, and_15_out, and_16_out, Clock_out,
       decoder_1_out0, decoder_1_out1, decoder_1_out2, decoder_1_out3, decoder_1_out4, decoder_1_out5,
       decoder_1_out6, decoder_1_out7, decoder_1_out8, decoder_1_out9, decoder_1_out10, decoder_1_out11,
       decoder_1_out12, decoder_1_out13, decoder_1_out14, decoder_1_out15;
  wire [15:0] register_1_q, register_2_q, register_3_q, register_4_q, register_5_q, register_6_q,
       register_7_q, register_8_q, register_9_q, register_10_q, register_11_q, register_12_q, register_13_q,
       register_14_q, register_15_q, register_16_q;

  Decoder #(.select(4), .enable("false")) decoder_1 (
    .out0(decoder_1_out0), .out1(decoder_1_out1), .out2(decoder_1_out2), .out3(decoder_1_out3),
    .out4(decoder_1_out4), .out5(decoder_1_out5), .out6(decoder_1_out6), .out7(decoder_1_out7),
    .out8(decoder_1_out8), .out9(decoder_1_out9), .out10(decoder_1_out10), .out11(decoder_1_out11),
    .out12(decoder_1_out12), .out13(decoder_1_out13), .out14(decoder_1_out14), .out15(decoder_1_out15),
    .sel(Write_Register));
  and and_1 (and_1_out, decoder_1_out0, Write_Control);
  and and_2 (and_2_out, decoder_1_out1, Write_Control);
  and and_3 (and_3_out, decoder_1_out2, Write_Control);
  and and_4 (and_4_out, decoder_1_out3, Write_Control);
  and and_5 (and_5_out, decoder_1_out4, Write_Control);
  and and_6 (and_6_out, decoder_1_out5, Write_Control);
  and and_7 (and_7_out, decoder_1_out6, Write_Control);
  and and_8 (and_8_out, decoder_1_out7, Write_Control);
  Register #(.width(16)) register_1 (.D(Write_Data), .en(and_1_out), .Q(register_1_q), .clk(Clock_out), .clr(Clear));
  Register #(.width(16)) register_2 (.D(Write_Data), .en(and_2_out), .Q(register_2_q), .clk(Clock_out), .clr(Clear));
  Register #(.width(16)) register_3 (.D(Write_Data), .en(and_3_out), .Q(register_3_q), .clk(Clock_out), .clr(Clear));
  Register #(.width(16)) register_4 (.D(Write_Data), .en(and_4_out), .Q(register_4_q), .clk(Clock_out), .clr(Clear));
  Register #(.width(16)) register_5 (.D(Write_Data), .en(and_5_out), .Q(register_5_q), .clk(Clock_out), .clr(Clear));
  Register #(.width(16)) register_6 (.D(Write_Data), .en(and_6_out), .Q(register_6_q), .clk(Clock_out), .clr(Clear));
  Register #(.width(16)) register_7 (.D(Write_Data), .en(and_7_out), .Q(register_7_q), .clk(Clock_out), .clr(Clear));
  Register #(.width(16)) register_8 (.D(Write_Data), .en(and_8_out), .Q(register_8_q), .clk(Clock_out), .clr(Clear));
  Clock Clock (.out(Clock_out));
  and and_9 (and_9_out, decoder_1_out8, Write_Control);
  and and_10 (and_10_out, decoder_1_out9, Write_Control);
  and and_11 (and_11_out, decoder_1_out10, Write_Control);
  and and_12 (and_12_out, decoder_1_out11, Write_Control);
  and and_13 (and_13_out, decoder_1_out12, Write_Control);
  and and_14 (and_14_out, decoder_1_out13, Write_Control);
  and and_15 (and_15_out, decoder_1_out14, Write_Control);
  and and_16 (and_16_out, decoder_1_out15, Write_Control);
  Register #(.width(16)) register_9 (.D(Write_Data), .en(and_9_out), .Q(register_9_q), .clk(Clock_out), .clr(Clear));
  Register #(.width(16)) register_10 (.D(Write_Data), .en(and_10_out), .Q(register_10_q), .clk(Clock_out), .clr(Clear));
  Register #(.width(16)) register_11 (.D(Write_Data), .en(and_11_out), .Q(register_11_q), .clk(Clock_out), .clr(Clear));
  Register #(.width(16)) register_12 (.D(Write_Data), .en(and_12_out), .Q(register_12_q), .clk(Clock_out), .clr(Clear));
  Register #(.width(16)) register_13 (.D(Write_Data), .en(and_13_out), .Q(register_13_q), .clk(Clock_out), .clr(Clear));
  Register #(.width(16)) register_14 (.D(Write_Data), .en(and_14_out), .Q(register_14_q), .clk(Clock_out), .clr(Clear));
  Register #(.width(16)) register_15 (.D(Write_Data), .en(and_15_out), .Q(register_15_q), .clk(Clock_out), .clr(Clear));
  Register #(.width(16)) register_16 (.D(Write_Data), .en(and_16_out), .Q(register_16_q), .clk(Clock_out), .clr(Clear));
  Multiplexer #(.select(4), .width(16), .enable("false")) multiplexer_1 (
    .in0(register_1_q), .in1(register_2_q), .in2(register_3_q), .in3(register_4_q), .in4(register_5_q),
    .in5(register_6_q), .in6(register_7_q), .in7(register_8_q), .in8(register_9_q), .in9(register_10_q),
    .in10(register_11_q), .in11(register_12_q), .in12(register_13_q), .in13(register_14_q),
    .in14(register_15_q), .in15(register_16_q), .out(Read_Data1), .sel(Read_Register1));
  Multiplexer #(.select(4), .width(16), .enable("false")) multiplexer_2 (
    .in0(register_1_q), .in1(register_2_q), .in2(register_3_q), .in3(register_4_q), .in4(register_5_q),
    .in5(register_6_q), .in6(register_7_q), .in7(register_8_q), .in8(register_9_q), .in9(register_10_q),
    .in10(register_11_q), .in11(register_12_q), .in12(register_13_q), .in13(register_14_q),
    .in14(register_15_q), .in15(register_16_q), .out(Read_Data2), .sel(Read_Register2));

  // Notes on the sheet:
  //   Najifa Tabassum
  //   2211578042
endmodule
