// Logisim project lab7.circ as structural Verilog: 1 circuit, main circuit main
module main (
);

  wire [15:0] adder_1_out, bit_extender_1_out, PC_q;

  assign bit_extender_1_out = {{15{1'b0}}, 1'b1};  // Bit_Extender bit_extender_1
  Register #(.width(16)) PC (.D(adder_1_out), .Q(PC_q));  // open: en, clk, clr
  Adder #(.width(16)) adder_1 (.a(bit_extender_1_out), .b(PC_q), .out(adder_1_out));  // open: cin, cout
  ROM #(.addrWidth(16), .dataWidth(16)) rom_1 (.addr(PC_q));  // open: data, sel
endmodule
